// Digital circuit alu.dig as structural Verilog
module alu (
  input  [3:0] AluOp,
  input  [15:0] Rhs,
  input  clk,
  input  [15:0] Lhs,
  output [15:0] Q
);

  wire [15:0] add_1_s, asr_out, lsr_out, shl_out, undriven;

  // And and_1 has open pins: In_1=undriven, In_2=Rhs, out=open
  // Or or_1 has open pins: In_1=undriven, In_2=Rhs, out=open
  // XOr xor_1 has open pins: In_1=undriven, In_2=Rhs, out=open
  Sub #(.Bits(16)) sub_1 (.a(undriven), .b(Rhs), .c_i(1'b0));  // open: s, c_o
  Add #(.Bits(16)) add_1 (.a(Lhs), .s(add_1_s));  // open: b, c_i, c_o
  BarrelShifter #(.Bits(16)) shl (.out(shl_out));  // open: in, shift
  BarrelShifter #(.Bits(16), .direction("right")) lsr (.out(lsr_out));  // open: in, shift
  BarrelShifter #(.Bits(16), .barrelShifterMode("arithmetic"), .direction("right")) asr (.out(asr_out));  // open: in, shift
  Multiplexer #(.Selector_Bits(2), .Bits(16)) multiplexer_1 (
    .in_0(add_1_s), .in_1(shl_out), .in_2(lsr_out), .in_3(asr_out));  // open: sel, out
endmodule
