// Digital circuit cpu.dig as structural Verilog
module cpu (
  input  clk
);

  wire alu_1_p4, decode_1_leftsel, decode_1_rightsel, Decode_Execute_p9, Decode_Execute_p10,
       Decode_Execute_p11, Decode_Execute_p12, Decode_Execute_p13, Decode_Execute_p14, Execute_Memory_p6,
       Execute_Memory_p7, fetch_1_p4, RegFile_p8, RegFile_p9, RegFile_p10;
  wire [1:0] decode_1_writebackmode, Execute_Memory_p8, Memory_Writeback_p5;
  wire [2:0] decode_1_jmpcond, decode_1_memorymode;
  wire [3:0] decode_1_alufunc;
  wire [15:0] decode_1_imm, Execute_Memory_p9, Execute_Memory_p10, fetch_1_p2, fetch_1_p3,
       Fetch_Decode_inst_2, Memory_Writeback_p6, Memory_Writeback_p7, RegFile_p7;

  // fetch fetch_1: pin names not known; wires that end beside it: clk, fetch_1_p2, fetch_1_p3, fetch_1_p4
  f_de Fetch_Decode (.Inst(fetch_1_p3), .clk(clk), .Inst_2(Fetch_Decode_inst_2));
  decode decode_1 (
    .Inst(Fetch_Decode_inst_2), .clk(clk), .WritebackMode(decode_1_writebackmode),
    .MemoryMode(decode_1_memorymode), .JmpCond(decode_1_jmpcond), .AluFunc(decode_1_alufunc),
    .RightSel(decode_1_rightsel), .LeftSel(decode_1_leftsel), .Imm(decode_1_imm));  // open: DestReg, SrcReg
  // operands RegFile: pin names not known; wires that end beside it: decode_1_rightsel, decode_1_leftsel, decode_1_imm, Memory_Writeback_p5[1], fetch_1_p4, clk, RegFile_p7, RegFile_p8, RegFile_p9, RegFile_p10
  // de_ex Decode_Execute: pin names not known; wires that end beside it: decode_1_writebackmode, decode_1_memorymode, decode_1_jmpcond, decode_1_alufunc, RegFile_p8, RegFile_p9, RegFile_p10, clk, Decode_Execute_p9, Decode_Execute_p10, Decode_Execute_p11, Decode_Execute_p12, Decode_Execute_p13, Decode_Execute_p14
  // alu alu_1: pin names not known; wires that end beside it: Decode_Execute_p11, Decode_Execute_p12, Decode_Execute_p13, alu_1_p4
  // ex_mem Execute_Memory: pin names not known; wires that end beside it: Decode_Execute_p9, Decode_Execute_p10, clk, alu_1_p4, Decode_Execute_p14, Execute_Memory_p6, Execute_Memory_p7, Execute_Memory_p8, Execute_Memory_p9, Execute_Memory_p10
  mem mem_1 (
    .MemRdEn(Execute_Memory_p7), .MemWrEn(Execute_Memory_p8), .DataIn(Execute_Memory_p9),
    .Addr(Execute_Memory_p10), .clk(clk), .Q(fetch_1_p2));
  // mem_wb Memory_Writeback: pin names not known; wires that end beside it: Execute_Memory_p6, clk, Execute_Memory_p10, fetch_1_p2, Memory_Writeback_p5, Memory_Writeback_p6, Memory_Writeback_p7
  Multiplexer #(.Bits(16)) multiplexer_1 (
    .sel(Memory_Writeback_p5[0]), .in_0(Memory_Writeback_p6), .in_1(Memory_Writeback_p7), .out(RegFile_p7));
endmodule
