// Digital circuit decode.dig as structural Verilog
module decode (
  input  [15:0] Inst,
  input  clk,
  output [1:0] WritebackMode,
  output [2:0] MemoryMode,
  output [2:0] JmpCond,
  output [3:0] AluFunc,
  output RightSel,
  output LeftSel,
  output [15:0] Imm,
  output [3:0] DestReg,
  output [3:0] SrcReg
);

  wire [31:11] rom_1_d;

  ROM #(.AddrBits(16), .Bits(32)) rom_1 (
    .A(Inst), .sel(1'b1),
    .D({rom_1_d[31:25], SrcReg, DestReg, JmpCond, rom_1_d[13:11], AluFunc, WritebackMode, MemoryMode, RightSel, LeftSel}));
  Multiplexer #(.Selector_Bits(3), .Bits(16)) multiplexer_1 (
    .sel(rom_1_d[13:11]), .in_0({Inst[8], Inst[14:9], Inst[7:4], {5{1'b0}}}),
    .in_1({{12{Inst[8]}}, Inst[11:9], Inst[12]}), .in_2({{12{Inst[8]}}, Inst[2:0], Inst[0]}),
    .in_3({{12{Inst[8]}}, Inst[7:4]}), .in_4({{10{Inst[8]}}, {2{Inst[3]}}, Inst[7:4]}),
    .in_5({11'h1, Inst[3:0], Inst[0]}), .in_6({16{1'b0}}), .in_7({16{1'b0}}), .out(Imm));

  // Notes on the sheet:
  //   clk: Hz: 400
  //   rom_1 loads decoder.bin
endmodule
