// Digital circuit ex_mem.dig as structural Verilog
module ex_mem (
  input  [1:0] WrBackEn,
  input  [2:0] MemMode,
  input  clk,
  input  [15:0] AluRes,
  input  [15:0] DataSrc,
  output [1:0] WrBackEn_2,
  output [2:0] MemMode_2,
  output [15:0] AluRes_2,
  output [15:0] DataSrc_2
);

  Register #(.Bits(16)) register_1 (.D(DataSrc), .C(clk), .en(1'b1), .Q(DataSrc_2));
  Register #(.Bits(16)) register_2 (.D(AluRes), .C(clk), .en(1'b1), .Q(AluRes_2));
  Register #(.Bits(3)) register_3 (.D(MemMode), .C(clk), .en(1'b1), .Q(MemMode_2));
  Register #(.Bits(2)) register_4 (.D(WrBackEn), .C(clk), .en(1'b1), .Q(WrBackEn_2));
endmodule
