// Digital circuit fetch.dig as structural Verilog
module fetch (
  input  FetchEn,
  input  JmpEn,
  input  [15:0] JmpDst,
  input  clk,
  input  [15:0] Mem,
  output [15:0] Inst,
  output [15:0] ProgCount
);

  wire or_1_out;
  wire [15:0] add_1_s, multiplexer_2_out;

  Multiplexer #(.Bits(16)) multiplexer_1 (.sel(FetchEn), .in_0({16{1'b0}}), .in_1(Mem), .out(Inst));
  or or_1 (or_1_out, JmpEn, FetchEn);
  Register #(.Bits(16)) Program_Counter (.D(multiplexer_2_out), .C(clk), .en(or_1_out), .Q(ProgCount));
  Multiplexer #(.Bits(16)) multiplexer_2 (.sel(JmpEn), .in_0(add_1_s), .in_1(JmpDst), .out(multiplexer_2_out));
  Add #(.Bits(16)) add_1 (.a(16'h2), .b(ProgCount), .c_i(1'b0), .s(add_1_s));  // open: c_o
endmodule
