// Digital circuit mem.dig as structural Verilog
module mem (
  input  [2:0] MemMode,
  input  [15:0] Addr,
  input  [15:0] DataIn,
  input  clk,
  output [15:0] Q
);

  wire [7:0] multiplexer_1_out;
  wire [15:0] bitextender_1_out, multiplexer_2_out, rom_1_d;

  ROM #(.AddrBits(16), .Bits(16)) rom_1 (.A(Addr), .sel(1'b1), .D(rom_1_d));
  Multiplexer #(.Bits(8)) multiplexer_1 (
    .sel(Addr[0]), .in_0(rom_1_d[7:0]), .in_1(rom_1_d[15:8]), .out(multiplexer_1_out));
  BitExtender bitextender_1 (.in(multiplexer_1_out), .out(bitextender_1_out));
  Multiplexer #(.Bits(16)) multiplexer_2 (
    .sel(1'b1), .in_0(bitextender_1_out), .in_1({{8{1'b0}}, multiplexer_1_out}), .out(multiplexer_2_out));
  Multiplexer #(.Bits(16)) multiplexer_3 (.sel(1'b1), .in_0(multiplexer_2_out), .in_1(rom_1_d), .out(Q));
endmodule
